# Fritzing sketch sketch (saved by Fritzing 0.9.3b)
breadboards: 1

parts:
  Part1 = Spark Core (v1.0)
  U1 = 8RelayModule

nets:
  GND: Part1.GND, U1.GND, U1.IN8
  VIN: Part1.VIN, U1.VCC
  N1: Part1.D1, U1.IN1
  N2: Part1.D2, U1.IN2
  N3: Part1.D3, U1.IN3
  N4: Part1.D4, U1.IN4
  N5: Part1.D5, U1.IN5
  N6: Part1.D6, U1.IN6
  N7: Part1.D7, U1.IN7

custom parts:
  8RelayModule: 8 relay arduino module SONGLE SRD05VDC-SL-C
